# Fritzing sketch PIoTDistanceBreadBoardWiringDiagram (saved by Fritzing 0.9.2b)
breadboards: 1

parts:
  Part1 = HC-SR04
  R1 = Resistor [tolerance=±5% resistance=1k package=THT]
  R2 = Resistor [tolerance=±5% resistance=1k package=THT]
  R3 = Resistor [tolerance=±5% resistance=1k package=THT]
  Pi1 = Adafruit Pi Cobbler

nets:
  N1: Part1.VCC, Pi1.5V0
  N2: Part1.Trig, Pi1.#23
  N3: Part1.Echo, R1.Pin_1
  GND: Part1.GND, R3.Pin_0, Pi1.GND
  N4: R1.Pin_0, R2.Pin_1, Pi1.#24
  N5: R2.Pin_0, R3.Pin_1

notes:
  PIoT Distance Wiring Diagram

custom parts:
  Adafruit Pi Cobbler: Adafruit Pi Cobbler GPIO Breakout for Raspberry Pi
